# Fritzing sketch rpi_water_pump (saved by Fritzing 0.9.3b)
breadboards: 1

parts:
  Raspberry_Pi1 = Raspberry Pi 2
  M1 = DC Motor
  J2 = Power Jack [package=power_jack_smd]
  KY-2 = Keyes Relay [package=THT]
  Q2 = TRANSISTOR_NPN [package=to-92-ammo]
  R3 = Resistor [tolerance=±5% resistance=1k package=THT]
  R4 = Resistor [tolerance=±5% resistance=10k package=THT]

nets:
  N1: Raspberry_Pi1.GPIO18, R3.Pin_0
  N2: Raspberry_Pi1.GND, KY-2.ground, Q2.E
  N3: Raspberry_Pi1.5V, KY-2.power, R4.Pin_1
  N4: M1.pin_1, J2.GNDBREAK
  N5: M1.pin_2, KY-2.C
  N6: J2.GND, KY-2.NC
  N7: KY-2.signal, Q2.C, R4.Pin_0
  N8: Q2.B, R3.Pin_1

notes:
  Transistor 2N2222
  Transistor 2N2222
  Rezistor 1k
  Rezistor 10k

custom parts:
  Keyes Relay: The Keyes 5V relay module is suitable for SCM development, home appliance control. It uses a 5V~12V TIL control signal which can control DC / AC signal.
